// Logisim project Addition and subtraction.circ as structural Verilog: 5 circuits, main circuit Final design Full adder and subtractor
module main (
  input  A1,
  input  A2,
  input  A3,
  input  A4,
  input  B1,
  input  B2,
  input  B3,
  input  B4,
  input  Control,
  output Sign,
  output S7,
  output S6,
  output S5,
  output S4,
  output S3,
  output S2,
  output S1
);

  wire adder_and_subtractor_1_control_2, adder_and_subtractor_1_s1, adder_and_subtractor_1_s2,
       adder_and_subtractor_1_s3, adder_and_subtractor_1_s4, n7404_1_p3, n7404_1_p7, n7486_1_p3, n7486_1_p6,
       n7486_1_p11, n74157_1_p2, n74157_1_p3;

  Adder_and_subtractor adder_and_subtractor_1 (
    .A1(A1), .A2(A2), .A3(A3), .A4(A4), .B1(B1), .B2(B2), .B3(B3), .B4(B4), .Control(Control),
    .S4(adder_and_subtractor_1_s4), .S3(adder_and_subtractor_1_s3), .S2(adder_and_subtractor_1_s2),
    .S1(adder_and_subtractor_1_s1), .Control_2(adder_and_subtractor_1_control_2));
  // _74157 74157_1: pin names not known; wires that end beside it: A4, n74157_1_p2, n74157_1_p3, Sign, 1'b1, 1'b0
  // _7404 7404_1: pin names not known; wires that end beside it: 1'b0, adder_and_subtractor_1_s4, n7404_1_p3, n74157_1_p2, n74157_1_p3, adder_and_subtractor_1_control_2, n7404_1_p7, 1'b0, 1'b1
  // _7408 7408_1: pin names not known; wires that end beside it: n7404_1_p3, adder_and_subtractor_1_control_2, n74157_1_p2, 1'b0, 1'b1, n7404_1_p7, adder_and_subtractor_1_s4, S4
  // _7486 7486_1: pin names not known; wires that end beside it: adder_and_subtractor_1_s3, n74157_1_p2, n7486_1_p3, adder_and_subtractor_1_s2, n74157_1_p2, n7486_1_p6, 1'b0, 1'b1, n74157_1_p2, adder_and_subtractor_1_s1, n7486_1_p11
  // _7483 7483_1: pin names not known; wires that end beside it: 1'b0, S3, n7486_1_p3, 1'b0, 1'b1, S2, 1'b0, n7486_1_p6, 1'b0, n74157_1_p2, 1'b0, 1'b0, n7486_1_p11, S1

  assign S5 = 1'b0;
  assign S6 = 1'b0;
  assign S7 = 1'b0;
endmodule

module _7485 (
  input  A4,
  input  B4,
  input  A3,
  input  B3,
  input  A_B,
  input  A_B_2,
  input  A_B_3,
  input  A2,
  input  B2,
  input  A1,
  input  B1,
  output A_B_4,
  output A_B_5,
  output A_B_6
);

  wire and_1_out, and_2_out, and_3_out, and_4_out, and_5_out, and_6_out, and_7_out, and_8_out, and_9_out,
       and_10_out, and_11_out, and_12_out, and_13_out, and_14_out, nor_1_out, nor_2_out, nor_3_out,
       nor_4_out, not_1_out, not_2_out, not_3_out, not_4_out, not_5_out, not_6_out, not_7_out, not_8_out;

  not not_1 (not_1_out, A4);
  not not_2 (not_2_out, B4);
  not not_3 (not_3_out, A3);
  not not_4 (not_4_out, B3);
  not not_5 (not_5_out, A2);
  not not_6 (not_6_out, B2);
  not not_7 (not_7_out, A1);
  not not_8 (not_8_out, B1);
  and and_1 (and_1_out, B4, not_1_out);
  and and_2 (and_2_out, A4, not_2_out);
  and and_3 (and_3_out, B3, not_3_out);
  and and_4 (and_4_out, not_4_out, A3);
  and and_5 (and_5_out, B2, not_5_out);
  and and_6 (and_6_out, A2, not_6_out);
  and and_7 (and_7_out, B1, not_7_out);
  and and_8 (and_8_out, not_8_out, A1);
  nor nor_1 (nor_1_out, and_1_out, and_2_out);
  nor nor_2 (nor_2_out, and_3_out, and_4_out);
  nor nor_3 (nor_3_out, and_5_out, and_6_out);
  nor nor_4 (nor_4_out, and_7_out, and_8_out);
  and and_9 (and_9_out, nor_1_out, and_3_out);
  and and_10 (and_10_out, nor_1_out, and_4_out);
  and and_11 (and_11_out, nor_1_out, nor_2_out, and_5_out);
  and and_12 (and_12_out, nor_1_out, nor_2_out, and_6_out);
  and and_13 (and_13_out, nor_1_out, nor_2_out, nor_3_out, and_7_out);
  and and_14 (and_14_out, nor_1_out, nor_2_out, nor_3_out, and_8_out);
  and and_15 (A_B_6, nor_1_out, nor_2_out, nor_3_out, nor_4_out);
  or or_1 (A_B_4, and_1_out, and_9_out, and_11_out, and_13_out);
  or or_2 (A_B_5, and_2_out, and_10_out, and_12_out, and_14_out);

  // Notes on the sheet:
  //   4-bit magnitude comparator 
endmodule

module Adder_and_subtractor (
  input  A1,
  input  A2,
  input  A3,
  input  A4,
  input  B1,
  input  B2,
  input  B3,
  input  B4,
  input  Control,
  output S4,
  output S3,
  output S2,
  output S1,
  output Control_2
);

  wire n7483_1_p4, n7483_1_p7, n7483_1_p14, n7486_2_p3;

  // _7483 7483_1: pin names not known; wires that end beside it: 1'b0, S3, A3, n7483_1_p4, 1'b1, S2, n7483_1_p7, A2, 1'b0, S4, 1'b0, Control_2, 1'b0, n7483_1_p14, A1, S1
  // _7486 7486_1: pin names not known; wires that end beside it: B1, Control_2, n7483_1_p14, B2, Control_2, n7483_1_p7, 1'b0, 1'b1, Control_2, B3, n7483_1_p4
  // _7486 7486_2: pin names not known; wires that end beside it: A4, B4, n7486_2_p3, n7486_2_p3, Control, Control_2, 1'b0, 1'b1

  // Notes on the sheet:
  //   Cin of adder 
  //   Power
  //   Ground
endmodule

module Full_adder_and_subtractor (
  input  A1,
  input  A2,
  input  A3,
  input  A4,
  input  B1,
  input  B2,
  input  B3,
  input  B4,
  input  Control,
  output Sign,
  output Carry,
  output S3,
  output S2,
  output S1
);

  wire _4_bit_comparator_a_b_4, _4_bit_comparator_a_b_5, Adder_and_subtractor_control_2,
       Adder_and_subtractor_s1, Adder_and_subtractor_s2, Adder_and_subtractor_s3, Adder_and_subtractor_s4,
       n7408_1_p2, n7408_1_p4, n7408_1_p6, n7408_1_p7, n7408_1_p11, n7408_1_p14, n7408_2_p3, n7408_2_p8,
       n7432_1_p3, n7483_1_p3, n7483_1_p8, n7483_1_p14, n7486_1_p3, n7486_1_p7, n7486_1_p9, n7486_3_p3;

  Adder_and_subtractor Adder_and_subtractor (
    .A1(A1), .A2(A2), .A3(A3), .A4(A4), .B1(B1), .B2(B2), .B3(B3), .B4(B4), .Control(Control),
    .S4(Adder_and_subtractor_s4), .S3(Adder_and_subtractor_s3), .S2(Adder_and_subtractor_s2),
    .S1(Adder_and_subtractor_s1), .Control_2(Adder_and_subtractor_control_2));
  _7485 _4_bit_comparator (
    .A4(1'b0), .B4(1'b0), .A3(A3), .B3(B3), .A_B(1'b0), .A_B_2(1'b0), .A_B_3(1'b0), .A2(A2), .B2(B2),
    .A1(A1), .B1(B1), .A_B_4(_4_bit_comparator_a_b_4), .A_B_5(_4_bit_comparator_a_b_5));  // open: A_B_6
  // _7486 7486_1: pin names not known; wires that end beside it: _4_bit_comparator_a_b_5, _4_bit_comparator_a_b_4, n7486_1_p3, 1'b1, Adder_and_subtractor_s4, Adder_and_subtractor_control_2, n7486_1_p7, Adder_and_subtractor_s4, n7486_1_p9
  // _7408 7408_1: pin names not known; wires that end beside it: 1'b0, n7408_1_p2, _4_bit_comparator_a_b_5, n7408_1_p4, n7408_1_p4, n7408_1_p6, n7408_1_p7, Carry, Adder_and_subtractor_control_2, A4, n7408_1_p11, n7408_1_p6, n7408_1_p11, n7408_1_p14
  // _7408 7408_2: pin names not known; wires that end beside it: n7486_1_p3, Adder_and_subtractor_control_2, n7408_2_p3, 1'b0, 1'b1, n7486_1_p7, _4_bit_comparator_a_b_4, n7408_2_p8, Adder_and_subtractor_s4, Adder_and_subtractor_control_2, n7486_1_p9
  // _7432 7432_1: pin names not known; wires that end beside it: n7408_2_p3, A4, n7432_1_p3, 1'b0, 1'b1
  // _7483 7483_1: pin names not known; wires that end beside it: 1'b0, S3, n7483_1_p3, 1'b0, 1'b1, S2, 1'b0, n7483_1_p8, 1'b0, 1'b0, n7408_2_p8, 1'b0, 1'b0, n7483_1_p14, S1
  // _7486 7486_2: pin names not known; wires that end beside it: Adder_and_subtractor_s2, n7408_2_p8, n7483_1_p8, Adder_and_subtractor_s3, n7408_2_p8, n7483_1_p3, 1'b0, 1'b1, Adder_and_subtractor_s1, n7408_2_p8, n7483_1_p14, n7432_1_p3, _4_bit_comparator_a_b_5, n7408_1_p6
  // _7486 7486_3: pin names not known; wires that end beside it: n7408_1_p7, n7408_1_p6, n7486_3_p3, n7408_1_p14, n7486_3_p3, Sign
  // _7404 7404_1: pin names not known; wires that end beside it: Adder_and_subtractor_control_2, n7408_1_p2
endmodule

module Final_design_Full_adder_and_subtractor (
  input  A1,
  input  A2,
  input  A3,
  input  A4,
  input  B1,
  input  B2,
  input  B3,
  input  B4,
  input  Control,
  output Sign,
  output S7,
  output S6,
  output S5,
  output S4,
  output S3,
  output S2,
  output S1
);

  wire adder_and_subtractor_1_control_2, adder_and_subtractor_1_s1, adder_and_subtractor_1_s2,
       adder_and_subtractor_1_s3, adder_and_subtractor_1_s4, n7404_1_p3, n7404_1_p7, n7486_1_p3, n7486_1_p6,
       n7486_1_p11, n74157_1_p2, n74157_1_p3;

  Adder_and_subtractor adder_and_subtractor_1 (
    .A1(A1), .A2(A2), .A3(A3), .A4(A4), .B1(B1), .B2(B2), .B3(B3), .B4(B4), .Control(Control),
    .S4(adder_and_subtractor_1_s4), .S3(adder_and_subtractor_1_s3), .S2(adder_and_subtractor_1_s2),
    .S1(adder_and_subtractor_1_s1), .Control_2(adder_and_subtractor_1_control_2));
  // _74157 74157_1: pin names not known; wires that end beside it: A4, n74157_1_p2, n74157_1_p3, Sign, 1'b1, 1'b0
  // _7404 7404_1: pin names not known; wires that end beside it: 1'b0, adder_and_subtractor_1_s4, n7404_1_p3, n74157_1_p2, n74157_1_p3, adder_and_subtractor_1_control_2, n7404_1_p7, 1'b0, 1'b1
  // _7408 7408_1: pin names not known; wires that end beside it: n7404_1_p3, adder_and_subtractor_1_control_2, n74157_1_p2, 1'b0, 1'b1, n7404_1_p7, adder_and_subtractor_1_s4, S4
  // _7486 7486_1: pin names not known; wires that end beside it: adder_and_subtractor_1_s3, n74157_1_p2, n7486_1_p3, adder_and_subtractor_1_s2, n74157_1_p2, n7486_1_p6, 1'b0, 1'b1, n74157_1_p2, adder_and_subtractor_1_s1, n7486_1_p11
  // _7483 7483_1: pin names not known; wires that end beside it: 1'b0, S3, n7486_1_p3, 1'b0, 1'b1, S2, 1'b0, n7486_1_p6, 1'b0, n74157_1_p2, 1'b0, 1'b0, n7486_1_p11, S1

  assign S5 = 1'b0;
  assign S6 = 1'b0;
  assign S7 = 1'b0;
endmodule
