// Logisim project Arithmatic unit.circ as structural Verilog: 1 circuit, main circuit main
module main (
  input  A1,
  input  A2,
  input  A3,
  input  A4,
  input  B1,
  input  B2,
  input  B3,
  input  B4,
  input  B,
  input  A,
  output Divide_by_Zero,
  output Zero_Divide,
  output Sign,
  output S8,
  output S7,
  output S6,
  output S5,
  output S4,
  output S3,
  output S2,
  output S1
);

  wire Addition_and_subtraction_s1, Addition_and_subtraction_s2, Addition_and_subtraction_s3,
       Addition_and_subtraction_s4, Addition_and_subtraction_sign, Division_divide_by_zero, Division_r1,
       Division_r2, Division_r3, Division_sign, Division_zero_divide, Multiplication_s1, Multiplication_s2,
       Multiplication_s3, Multiplication_s4, Multiplication_s5, Multiplication_s6, Multiplication_sign;

  Addition_and_subtraction_main Addition_and_subtraction (
    .A1(A1), .A2(A2), .A3(A3), .A4(A4), .B1(B1), .B2(B2), .B3(B3), .B4(B4), .Control(A),
    .Sign(Addition_and_subtraction_sign), .S4(Addition_and_subtraction_s4), .S3(Addition_and_subtraction_s3),
    .S2(Addition_and_subtraction_s2), .S1(Addition_and_subtraction_s1));  // open: S7, S6, S5
  Final_divider_circuit Division (
    .A1(A1), .A2(A2), .A3(A3), .A4(A4), .B1(B1), .B2(B2), .B3(B3), .B4(B4), .R1(Division_r1),
    .R2(Division_r2), .R3(Division_r3), .Sign(Division_sign), .Zero_divide(Division_zero_divide),
    .Divide_by_Zero(Division_divide_by_zero));
  Multiplication_under_progress_main Multiplication (
    .A1(A1), .A2(A2), .A3(A3), .B1(B1), .B2(B2), .B3(B3), .A4(A4), .B4(B4), .S1(Multiplication_s1),
    .S2(Multiplication_s2), .S3(Multiplication_s3), .S4(Multiplication_s4), .S5(Multiplication_s5),
    .S6(Multiplication_s6), .Sign(Multiplication_sign));
  // _74153 74153_1: pin names not known; wires that end beside it: 1'b0, B, Division_r1, Multiplication_s1, Addition_and_subtraction_s1, Addition_and_subtraction_s1, S1, 1'b0, 1'b1, 1'b0, A, Division_r2, Multiplication_s2, Addition_and_subtraction_s2, Addition_and_subtraction_s2, S2
  // _74153 74153_2: pin names not known; wires that end beside it: 1'b0, B, Division_r3, Multiplication_s3, Addition_and_subtraction_s3, Addition_and_subtraction_s3, S3, 1'b0, 1'b1, 1'b0, A, 1'b0, Multiplication_s4, Addition_and_subtraction_s4, Addition_and_subtraction_s4, S4
  // _74153 74153_3: pin names not known; wires that end beside it: 1'b0, B, 1'b0, Multiplication_s5, 1'b0, 1'b0, S5, 1'b0, 1'b1, 1'b0, A, 1'b0, Multiplication_s6, 1'b0, 1'b0, S6
  // _74153 74153_4: pin names not known; wires that end beside it: 1'b0, B, Division_sign, Multiplication_sign, Addition_and_subtraction_sign, Addition_and_subtraction_sign, Sign, 1'b0, 1'b1, 1'b0, A, Division_divide_by_zero, 1'b0, 1'b0, 1'b0, Divide_by_Zero
  // _74153 74153_5: pin names not known; wires that end beside it: 1'b0, B, Division_zero_divide, 1'b0, 1'b0, 1'b0, Zero_Divide, 1'b0, 1'b1, 1'b0, A

  assign S7 = 1'b0;
  assign S8 = 1'b0;
endmodule
