// Logisim project Converter Circuit.circ as structural Verilog: 6 circuits, main circuit 3 Input OR IC
// OR IC
module _3_Input_OR_IC (
  input  _1,
  input  _2,
  input  _3,
  input  _1_2,
  input  _2_2,
  input  _3_2,
  input  _1_3,
  input  _2_3,
  input  _3_3,
  output O1,
  output O2,
  output O3
);

  _3_input_or u_3_input_or_1 (.I0(_1), .I1(_2), .I2(_3), .out_4(O1));
  _3_input_or u_3_input_or_2 (.I0(_1_2), .I1(_2_2), .I2(_3_2), .out_4(O2));
  _3_input_or u_3_input_or_3 (.I0(_1_3), .I1(_2_3), .I2(_3_3), .out_4(O3));
endmodule

// OR
module _3_input_or (
  input  I0,
  input  I1,
  input  I2,
  output out_4
);

  or or_1 (out_4, I0, I1, I2);
endmodule

module _3_Input_And (
  input  _1,
  input  _2,
  input  _3,
  output out_4
);

  and and_1 (out_4, _1, _2, _3);
endmodule

module Main (
  input  A0,
  input  A1,
  input  A2,
  input  A3,
  output S3,
  output S2,
  output S1,
  output S0
);

  wire n3_input_and_ic_1_o1, n3_input_and_ic_1_o2, n3_input_and_ic_1_o3, n7404_1_p2, n7404_1_p4, n7404_1_p10,
       n7408_1_p3, n7408_1_p6, n7408_1_p11, n7408_1_p12, n7408_1_p14, n7408_2_p3, n7408_2_p6, n7408_2_p11;

  _3_Input_OR_IC u_3_input_or_ic_1 (
    ._1(A3), ._2(n7408_1_p3), ._3(n7408_1_p6), ._1_2(n7408_1_p11), ._2_2(n3_input_and_ic_1_o1), ._3_2(1'b0),
    ._1_3(n7408_1_p14), ._2_3(n7408_2_p3), ._3_3(n7408_2_p6), .O1(S3), .O2(S2), .O3(S1));
  // _7408 7408_1: pin names not known; wires that end beside it: A0, A2, n7408_1_p3, A2, A1, n7408_1_p6, 1'b0, 1'b1, A3, A0, n7408_1_p11, n7408_1_p12, A1, n7408_1_p14
  _3_Input_And_IC u_3_input_and_ic_1 (
    ._1(A2), ._2(n7404_1_p2), ._3(n7404_1_p4), ._1_2(n7404_1_p10), ._2_2(n7408_1_p12), ._3_2(A0), ._1_3(A2),
    ._2_3(A1), ._3_3(n7404_1_p4), .o1(n3_input_and_ic_1_o1), .o2(n3_input_and_ic_1_o2),
    .o3(n3_input_and_ic_1_o3));
  // _7404 7404_1: pin names not known; wires that end beside it: A1, n7404_1_p2, A0, n7404_1_p4, A2, n7408_1_p12, 1'b0, 1'b1, A3, n7404_1_p10
  // _7408 7408_2: pin names not known; wires that end beside it: A1, A0, n7408_2_p3, A3, A0, n7408_2_p6, 1'b0, 1'b1, A3, A0, n7408_2_p11
  _3_Input_OR_IC u_3_input_or_ic_2 (
    ._1(n7408_2_p11), ._2(n3_input_and_ic_1_o2), ._3(n3_input_and_ic_1_o3), .O1(S0));  // open: _1_2, _2_2, _3_2, _1_3, _2_3, _3_3, O2, O3
endmodule

// AND IC
module _3_Input_And_IC (
  input  _1,
  input  _2,
  input  _3,
  input  _1_2,
  input  _2_2,
  input  _3_2,
  input  _1_3,
  input  _2_3,
  input  _3_3,
  output o1,
  output o2,
  output o3
);

  _3_Input_And u_3_input_and_1 (._1(_1), ._2(_2), ._3(_3), .out_4(o1));
  _3_Input_And u_3_input_and_2 (._1(_1_2), ._2(_2_2), ._3(_3_2), .out_4(o2));
  _3_Input_And u_3_input_and_3 (._1(_1_3), ._2(_2_3), ._3(_3_3), .out_4(o3));
endmodule

module Converter (
  input  B0,
  input  B1,
  input  B2,
  input  B3,
  input  B4,
  input  B5,
  input  B6,
  input  B7,
  output P0,
  output P1,
  output P2,
  output P3,
  output P4,
  output P5,
  output P6,
  output P7,
  output P8,
  output P9
);

  wire main_1_s0, main_1_s1, main_1_s2, main_1_s3, main_2_s0, main_2_s1, main_2_s2, main_2_s3, main_3_s0,
       main_3_s1, main_3_s2, main_3_s3, main_4_s0, main_4_s1, main_4_s2, main_4_s3, main_5_s0, main_5_s1,
       main_5_s2;

  Main main_1 (.A0(B5), .A1(B6), .A2(B7), .A3(1'b0), .S3(main_1_s3), .S2(main_1_s2), .S1(main_1_s1), .S0(main_1_s0));
  Main main_2 (
    .A0(B4), .A1(main_1_s0), .A2(main_1_s1), .A3(main_1_s2), .S3(main_2_s3), .S2(main_2_s2), .S1(main_2_s1),
    .S0(main_2_s0));
  Main main_3 (
    .A0(B3), .A1(main_2_s0), .A2(main_2_s1), .A3(main_2_s2), .S3(main_3_s3), .S2(main_3_s2), .S1(main_3_s1),
    .S0(main_3_s0));
  Main main_4 (
    .A0(B2), .A1(main_3_s0), .A2(main_3_s1), .A3(main_3_s2), .S3(main_4_s3), .S2(main_4_s2), .S1(main_4_s1),
    .S0(main_4_s0));
  Main main_5 (
    .A0(main_3_s3), .A1(main_2_s3), .A2(main_1_s3), .A3(1'b0), .S3(P9), .S2(main_5_s2), .S1(main_5_s1),
    .S0(main_5_s0));
  Main main_6 (.A0(B1), .A1(main_4_s0), .A2(main_4_s1), .A3(main_4_s2), .S3(P4), .S2(P3), .S1(P2), .S0(P1));
  Main main_7 (.A0(main_4_s3), .A1(main_5_s0), .A2(main_5_s1), .A3(main_5_s2), .S3(P8), .S2(P7), .S1(P6), .S0(P5));

  assign P0 = B0;
endmodule
