// Logisim project Full integrated arithmatic unit.circ as structural Verilog: 1 circuit, main circuit main
module main (
  input  A1,
  input  A2,
  input  A3,
  input  A4,
  input  B1,
  input  B2,
  input  B3,
  input  B4,
  input  B,
  input  A
);

  wire AU_divide_by_zero, AU_s1, AU_s2, AU_s3, AU_s4, AU_s5, AU_s6, AU_s7, AU_s8, AU_sign, AU_zero_divide,
       Binary_to_BCD_converter_p0, Binary_to_BCD_converter_p1, Binary_to_BCD_converter_p2,
       Binary_to_BCD_converter_p3, Binary_to_BCD_converter_p4, Binary_to_BCD_converter_p5,
       Binary_to_BCD_converter_p6, Binary_to_BCD_converter_p7, n7448_1_p9, n7448_1_p10, n7448_1_p11,
       n7448_1_p12, n7448_1_p13, n7448_1_p14, n7448_2_p10, n7448_2_p12, n7448_2_p13, n7448_2_p14,
       n7448_2_p15, n7448_2_p16, n7448_2_p17, n7448_2_p18;

  Arithmatic_unit_main AU (
    .A1(A1), .A2(A2), .A3(A3), .A4(A4), .B1(B1), .B2(B2), .B3(B3), .B4(B4), .B(B), .A(A),
    .Divide_by_Zero(AU_divide_by_zero), .Zero_Divide(AU_zero_divide), .Sign(AU_sign), .S8(AU_s8), .S7(AU_s7),
    .S6(AU_s6), .S5(AU_s5), .S4(AU_s4), .S3(AU_s3), .S2(AU_s2), .S1(AU_s1));
  Converter Binary_to_BCD_converter (
    .B0(AU_s1), .B1(AU_s2), .B2(AU_s3), .B3(AU_s4), .B4(AU_s5), .B5(AU_s6), .B6(AU_s7), .B7(AU_s8),
    .P0(Binary_to_BCD_converter_p0), .P1(Binary_to_BCD_converter_p1), .P2(Binary_to_BCD_converter_p2),
    .P3(Binary_to_BCD_converter_p3), .P4(Binary_to_BCD_converter_p4), .P5(Binary_to_BCD_converter_p5),
    .P6(Binary_to_BCD_converter_p6), .P7(Binary_to_BCD_converter_p7));  // open: P8, P9
  // _7448 7448_1: pin names not known; wires that end beside it: Binary_to_BCD_converter_p5, Binary_to_BCD_converter_p6, 1'b1, 1'b0, 1'b1, Binary_to_BCD_converter_p7, Binary_to_BCD_converter_p4, 1'b1, n7448_1_p9, n7448_1_p10, n7448_1_p11, n7448_1_p12, n7448_1_p13, n7448_1_p14
  // _7448 7448_2: pin names not known; wires that end beside it: 1'b0, Binary_to_BCD_converter_p1, Binary_to_BCD_converter_p2, 1'b1, 1'b0, 1'b1, Binary_to_BCD_converter_p3, Binary_to_BCD_converter_p0, 1'b0, n7448_2_p10, 1'b1, n7448_2_p12, n7448_2_p13, n7448_2_p14, n7448_2_p15, n7448_2_p16, n7448_2_p17, n7448_2_p18
  LED led_1 (.in(AU_divide_by_zero));
  LED led_2 (.in(AU_zero_divide));
  LED led_3 (.in(AU_sign));
  _7_Segment_Display u_7_segment_display_1 (
    .g(n7448_1_p10), .f(n7448_1_p9), .a(n7448_1_p11), .b(n7448_1_p12), .e(n7448_2_p10), .d(n7448_1_p14),
    .c(n7448_1_p13));  // open: dp
  _7_Segment_Display u_7_segment_display_2 (
    .g(n7448_2_p13), .f(n7448_2_p12), .a(n7448_2_p14), .b(n7448_2_p15), .e(n7448_2_p18), .d(n7448_2_p17),
    .c(n7448_2_p16));  // open: dp

  // Notes on the sheet:
  //   Tenths
  //   Units 
endmodule
