// Logisim project Multiplication under progress.circ as structural Verilog: 2 circuits, main circuit main
// Divide by zero
module main (
  input  A1,
  input  A2,
  input  A3,
  input  B1,
  input  B2,
  input  B3,
  input  A4,
  input  B4,
  output S1,
  output S2,
  output S3,
  output S4,
  output S5,
  output S6,
  output Sign
);

  wire main_1__2__s3, main_1__6__s2, main_1__14__cout, main_1__15__s4, n7408_1_p6, n7408_1_p9, n7408_1_p14,
       n7408_1_p17, n7408_2_p3, n7408_2_p6, n7408_2_p11, n7408_2_p14, n7408_3_p3;

  // _7408 7408_1: pin names not known; wires that end beside it: A1, A2, A3, A1, B1, n7408_1_p6, A2, B1, n7408_1_p9, 1'b0, 1'b1, A3, B1, n7408_1_p14, A1, B2, n7408_1_p17
  // _7408 7408_2: pin names not known; wires that end beside it: A2, B2, n7408_2_p3, B2, A3, n7408_2_p6, 1'b0, 1'b1, A1, B3, n7408_2_p11, A2, B3, n7408_2_p14
  // _7408 7408_3: pin names not known; wires that end beside it: A3, B3, n7408_3_p3, 1'b0, 1'b1
  // _7486 7486_1: pin names not known; wires that end beside it: A4, B4, Sign, 1'b0, 1'b1
  full_adder_4_bit_main main_1 (
    ._1__A4(1'b0), ._2__S3(main_1__2__s3), ._3__A3(n7408_1_p14), ._4__B3(n7408_2_p3), ._5__VCC(1'b1),
    ._6__S2(main_1__6__s2), ._7__B2(n7408_1_p17), ._8__A2(n7408_1_p9), ._16__B4(n7408_2_p6),
    ._15__S4(main_1__15__s4), ._14__Cout(main_1__14__cout), ._13__Cin(1'b0), ._12__GND(1'b0), ._11__B1(1'b0),
    ._10__A1(n7408_1_p6), ._9__S1(S1));
  full_adder_4_bit_main main_2 (
    ._1__A4(main_1__14__cout), ._2__S3(S4), ._3__A3(main_1__15__s4), ._4__B3(n7408_2_p14), ._5__VCC(1'b1),
    ._6__S2(S3), ._7__B2(n7408_2_p11), ._8__A2(main_1__2__s3), ._16__B4(n7408_3_p3), ._15__S4(S5),
    ._14__Cout(S6), ._13__Cin(1'b0), ._12__GND(1'b0), ._11__B1(1'b0), ._10__A1(main_1__6__s2), ._9__S1(S2));
endmodule

module _7485 (
  input  A4,
  input  B4,
  input  A3,
  input  B3,
  input  A_B,
  input  A_B_2,
  input  A_B_3,
  input  A2,
  input  B2,
  input  A1,
  input  B1,
  output A_B_4,
  output A_B_5,
  output A_B_6
);

  wire and_1_out, and_2_out, and_3_out, and_4_out, and_5_out, and_6_out, and_7_out, and_8_out, and_9_out,
       and_10_out, and_11_out, and_12_out, and_13_out, and_14_out, nor_1_out, nor_2_out, nor_3_out,
       nor_4_out, not_1_out, not_2_out, not_3_out, not_4_out, not_5_out, not_6_out, not_7_out, not_8_out;

  not not_1 (not_1_out, A4);
  not not_2 (not_2_out, B4);
  not not_3 (not_3_out, A3);
  not not_4 (not_4_out, B3);
  not not_5 (not_5_out, A2);
  not not_6 (not_6_out, B2);
  not not_7 (not_7_out, A1);
  not not_8 (not_8_out, B1);
  and and_1 (and_1_out, B4, not_1_out);
  and and_2 (and_2_out, A4, not_2_out);
  and and_3 (and_3_out, B3, not_3_out);
  and and_4 (and_4_out, not_4_out, A3);
  and and_5 (and_5_out, B2, not_5_out);
  and and_6 (and_6_out, A2, not_6_out);
  and and_7 (and_7_out, B1, not_7_out);
  and and_8 (and_8_out, not_8_out, A1);
  nor nor_1 (nor_1_out, and_1_out, and_2_out);
  nor nor_2 (nor_2_out, and_3_out, and_4_out);
  nor nor_3 (nor_3_out, and_5_out, and_6_out);
  nor nor_4 (nor_4_out, and_7_out, and_8_out);
  and and_9 (and_9_out, nor_1_out, and_3_out);
  and and_10 (and_10_out, nor_1_out, and_4_out);
  and and_11 (and_11_out, nor_1_out, nor_2_out, and_5_out);
  and and_12 (and_12_out, nor_1_out, nor_2_out, and_6_out);
  and and_13 (and_13_out, nor_1_out, nor_2_out, nor_3_out, and_7_out);
  and and_14 (and_14_out, nor_1_out, nor_2_out, nor_3_out, and_8_out);
  and and_15 (A_B_6, nor_1_out, nor_2_out, nor_3_out, nor_4_out);
  or or_1 (A_B_4, and_1_out, and_9_out, and_11_out, and_13_out);
  or or_2 (A_B_5, and_2_out, and_10_out, and_12_out, and_14_out);

  // Notes on the sheet:
  //   4-bit magnitude comparator 
endmodule
