// Logisim project division under progress.circ as structural Verilog: 3 circuits, main circuit main
module main (
  input  A1,
  input  A2,
  input  A3,
  input  A4,
  input  B1,
  input  B2,
  input  B3,
  input  B4,
  output Q3,
  output Q2,
  output Q1,
  output R1,
  output R2,
  output R3,
  output Sign
);

  wire main_1__2__s3, main_1__6__s2, main_1__9__s1, main_2__2__s3, main_2__6__s2, main_2__9__s1,
       main_3__2__s3, main_3__6__s2, main_3__9__s1, n7404_1_p4, n7404_1_p6, n7404_1_p8, n74157_1_p4,
       n74157_1_p7, n74157_2_p4, n74157_2_p7;

  // _7404 7404_1: pin names not known; wires that end beside it: 1'b0, 1'b1, B1, n7404_1_p4, B2, n7404_1_p6, B3, n7404_1_p8
  full_adder_4_bit_main main_1 (
    ._1__A4(1'b0), ._2__S3(main_1__2__s3), ._3__A3(1'b0), ._4__B3(n7404_1_p8), ._5__VCC(1'b1),
    ._6__S2(main_1__6__s2), ._7__B2(n7404_1_p6), ._8__A2(1'b0), ._16__B4(1'b0), ._15__S4(Q3),
    ._13__Cin(1'b1), ._12__GND(1'b0), ._11__B1(n7404_1_p4), ._10__A1(A3), ._9__S1(main_1__9__s1));  // open: _14__Cout
  full_adder_4_bit_main main_2 (
    ._1__A4(1'b0), ._2__S3(main_2__2__s3), ._3__A3(n74157_1_p7), ._4__B3(n7404_1_p8), ._5__VCC(1'b1),
    ._6__S2(main_2__6__s2), ._7__B2(n7404_1_p6), ._8__A2(n74157_1_p4), ._16__B4(1'b0), ._15__S4(Q2),
    ._13__Cin(1'b1), ._12__GND(1'b0), ._11__B1(n7404_1_p4), ._10__A1(A2), ._9__S1(main_2__9__s1));  // open: _14__Cout
  full_adder_4_bit_main main_3 (
    ._1__A4(1'b0), ._2__S3(main_3__2__s3), ._3__A3(n74157_2_p7), ._4__B3(n7404_1_p8), ._5__VCC(1'b1),
    ._6__S2(main_3__6__s2), ._7__B2(n7404_1_p6), ._8__A2(n74157_2_p4), ._16__B4(1'b0), ._15__S4(Q1),
    ._13__Cin(1'b1), ._12__GND(1'b0), ._11__B1(n7404_1_p4), ._10__A1(A1), ._9__S1(main_3__9__s1));  // open: _14__Cout
  // _74157 74157_1: pin names not known; wires that end beside it: Q3, A3, main_1__9__s1, n74157_1_p4, 1'b0, main_1__6__s2, n74157_1_p7, 1'b0, 1'b1, 1'b0, 1'b0, main_1__2__s3
  // _74157 74157_2: pin names not known; wires that end beside it: Q2, A2, main_2__9__s1, n74157_2_p4, n74157_1_p4, main_2__6__s2, n74157_2_p7, 1'b0, 1'b1, 1'b0, n74157_1_p7, main_2__2__s3
  // _74157 74157_3: pin names not known; wires that end beside it: Q1, A1, main_3__9__s1, R1, n74157_2_p4, main_3__6__s2, R2, 1'b0, 1'b1, 1'b0, n74157_2_p7, main_3__2__s3, R3
  // _7486 7486_1: pin names not known; wires that end beside it: A4, B4, Sign
endmodule

module _7485 (
  input  A4,
  input  B4,
  input  A3,
  input  B3,
  input  A_B,
  input  A_B_2,
  input  A_B_3,
  input  A2,
  input  B2,
  input  A1,
  input  B1,
  output A_B_4,
  output A_B_5,
  output A_B_6
);

  wire and_1_out, and_2_out, and_3_out, and_4_out, and_5_out, and_6_out, and_7_out, and_8_out, and_9_out,
       and_10_out, and_11_out, and_12_out, and_13_out, and_14_out, nor_1_out, nor_2_out, nor_3_out,
       nor_4_out, not_1_out, not_2_out, not_3_out, not_4_out, not_5_out, not_6_out, not_7_out, not_8_out;

  not not_1 (not_1_out, A4);
  not not_2 (not_2_out, B4);
  not not_3 (not_3_out, A3);
  not not_4 (not_4_out, B3);
  not not_5 (not_5_out, A2);
  not not_6 (not_6_out, B2);
  not not_7 (not_7_out, A1);
  not not_8 (not_8_out, B1);
  and and_1 (and_1_out, B4, not_1_out);
  and and_2 (and_2_out, A4, not_2_out);
  and and_3 (and_3_out, B3, not_3_out);
  and and_4 (and_4_out, not_4_out, A3);
  and and_5 (and_5_out, B2, not_5_out);
  and and_6 (and_6_out, A2, not_6_out);
  and and_7 (and_7_out, B1, not_7_out);
  and and_8 (and_8_out, not_8_out, A1);
  nor nor_1 (nor_1_out, and_1_out, and_2_out);
  nor nor_2 (nor_2_out, and_3_out, and_4_out);
  nor nor_3 (nor_3_out, and_5_out, and_6_out);
  nor nor_4 (nor_4_out, and_7_out, and_8_out);
  and and_9 (and_9_out, nor_1_out, and_3_out);
  and and_10 (and_10_out, nor_1_out, and_4_out);
  and and_11 (and_11_out, nor_1_out, nor_2_out, and_5_out);
  and and_12 (and_12_out, nor_1_out, nor_2_out, and_6_out);
  and and_13 (and_13_out, nor_1_out, nor_2_out, nor_3_out, and_7_out);
  and and_14 (and_14_out, nor_1_out, nor_2_out, nor_3_out, and_8_out);
  and and_15 (A_B_6, nor_1_out, nor_2_out, nor_3_out, nor_4_out);
  or or_1 (A_B_4, and_1_out, and_9_out, and_11_out, and_13_out);
  or or_2 (A_B_5, and_2_out, and_10_out, and_12_out, and_14_out);

  // Notes on the sheet:
  //   4-bit magnitude comparator 
endmodule

module Final_divider_circuit (
  input  A1,
  input  A2,
  input  A3,
  input  A4,
  input  B1,
  input  B2,
  input  B3,
  input  B4,
  output R1,
  output R2,
  output R3,
  output Sign,
  output Zero_divide,
  output Divide_by_Zero
);

  main main_1 (
    .A1(A1), .A2(A2), .A3(A3), .A4(A4), .B1(B1), .B2(B2), .B3(B3), .B4(B4), .R1(R1), .R2(R2), .R3(R3),
    .Sign(Sign));  // open: Q3, Q2, Q1
  _7485 u_7485_1 (
    .A4(1'b0), .B4(1'b0), .A3(A3), .B3(1'b0), .A2(A2), .B2(1'b0), .A1(A1), .B1(1'b0), .A_B_6(Zero_divide));  // open: A_B, A_B_2, A_B_3, A_B_4, A_B_5
  _7485 u_7485_2 (
    .A4(1'b0), .B4(1'b0), .A3(B1), .B3(1'b0), .A2(B2), .B2(1'b0), .A1(B3), .B1(1'b0), .A_B_6(Divide_by_Zero));  // open: A_B, A_B_2, A_B_3, A_B_4, A_B_5
endmodule
